// Logisim project DecodeLab6.circ as structural Verilog: 6 circuits, main circuit Decode
module Decode (
  input  Cnd,
  input  [3:0] icode,
  input  [63:0] valE,
  input  [3:0] rA,
  input  [63:0] valM,
  input  [3:0] rB,
  output [63:0] valA,
  output [63:0] valB
);

  wire clk_out;
  wire [3:0] dste_1_dst_e, dstm_1_dst_m, srca_1_src_a, srcb_1_src_b;

  dstE dste_1 (.Cnd(Cnd), .icode(icode), .rB(rB), .dst_E(dste_1_dst_e));
  dstM dstm_1 (.icode(icode), .rA(rA), .dst_M(dstm_1_dst_m));
  srcA srca_1 (.icode(icode), .rA(rA), .src_A(srca_1_src_a));
  srcB srcb_1 (.icode(icode), .rB(rB), .src_B(srcb_1_src_b));
  Clock clk (.out(clk_out));
  Regsiterfile regsiterfile_1 (
    .valE(valE), .valM(valM), .dstE(dste_1_dst_e), .dstM(dstm_1_dst_m), .srcA(srca_1_src_a),
    .srcB(srcb_1_src_b), .clk(clk_out), .valA(valA), .valB(valB));
endmodule

module Regsiterfile (
  input  [63:0] valE,
  input  [63:0] valM,
  input  [3:0] dstE,
  input  [3:0] dstM,
  input  [3:0] srcA,
  input  [3:0] srcB,
  input  clk,
  output [63:0] valA,
  output [63:0] valB
);

  wire decoder_1_out0, decoder_1_out1, decoder_1_out2, decoder_1_out3, decoder_1_out4, decoder_1_out5,
       decoder_1_out6, decoder_1_out7, decoder_1_out8, decoder_1_out9, decoder_1_out10, decoder_1_out11,
       decoder_1_out12, decoder_1_out13, decoder_1_out14, decoder_2_out0, decoder_2_out1, decoder_2_out2,
       decoder_2_out3, decoder_2_out4, decoder_2_out5, decoder_2_out6, decoder_2_out7, decoder_2_out8,
       decoder_2_out9, decoder_2_out10, decoder_2_out11, decoder_2_out12, decoder_2_out13, decoder_2_out14,
       or_1_out, or_2_out, or_3_out, or_4_out, or_5_out, or_6_out, or_7_out, or_8_out, or_9_out, or_10_out,
       or_11_out, or_12_out, or_13_out, or_14_out, or_15_out;
  wire [63:0] multiplexer_1_out, multiplexer_2_out, multiplexer_3_out, multiplexer_4_out, multiplexer_5_out,
       multiplexer_6_out, multiplexer_7_out, multiplexer_8_out, multiplexer_9_out, multiplexer_10_out,
       multiplexer_11_out, multiplexer_12_out, multiplexer_13_out, multiplexer_14_out, multiplexer_15_out,
       r8_q, r9_q, r10_q, r11_q, r12_q, r13_q, r14_q, rax_q, rbp_q, rbx_q, rcx_q, rdi_q, rdx_q, rsi_q, rsp_q;

  Decoder #(.select(4)) decoder_1 (
    .out0(decoder_1_out0), .out1(decoder_1_out1), .out2(decoder_1_out2), .out3(decoder_1_out3),
    .out4(decoder_1_out4), .out5(decoder_1_out5), .out6(decoder_1_out6), .out7(decoder_1_out7),
    .out8(decoder_1_out8), .out9(decoder_1_out9), .out10(decoder_1_out10), .out11(decoder_1_out11),
    .out12(decoder_1_out12), .out13(decoder_1_out13), .out14(decoder_1_out14), .sel(dstE), .en(1'b1));  // open: out15
  Decoder #(.select(4)) decoder_2 (
    .out0(decoder_2_out0), .out1(decoder_2_out1), .out2(decoder_2_out2), .out3(decoder_2_out3),
    .out4(decoder_2_out4), .out5(decoder_2_out5), .out6(decoder_2_out6), .out7(decoder_2_out7),
    .out8(decoder_2_out8), .out9(decoder_2_out9), .out10(decoder_2_out10), .out11(decoder_2_out11),
    .out12(decoder_2_out12), .out13(decoder_2_out13), .out14(decoder_2_out14), .sel(dstM), .en(1'b1));  // open: out15
  or or_1 (or_1_out, decoder_1_out0, decoder_2_out0);
  or or_2 (or_2_out, decoder_1_out1, decoder_2_out1);
  or or_3 (or_3_out, decoder_1_out2, decoder_2_out2);
  or or_4 (or_4_out, decoder_1_out3, decoder_2_out3);
  or or_5 (or_5_out, decoder_1_out4, decoder_2_out4);
  or or_6 (or_6_out, decoder_1_out5, decoder_2_out5);
  or or_7 (or_7_out, decoder_1_out6, decoder_2_out6);
  or or_8 (or_8_out, decoder_1_out7, decoder_2_out7);
  or or_9 (or_9_out, decoder_1_out8, decoder_2_out8);
  or or_10 (or_10_out, decoder_1_out9, decoder_2_out9);
  or or_11 (or_11_out, decoder_1_out10, decoder_2_out10);
  or or_12 (or_12_out, decoder_1_out11, decoder_2_out11);
  or or_13 (or_13_out, decoder_1_out12, decoder_2_out12);
  or or_14 (or_14_out, decoder_1_out13, decoder_2_out13);
  or or_15 (or_15_out, decoder_1_out14, decoder_2_out14);
  Multiplexer #(.width(64)) multiplexer_1 (.in0(valM), .in1(valE), .out(multiplexer_1_out), .sel(decoder_1_out0));
  Multiplexer #(.width(64)) multiplexer_2 (.in0(valM), .in1(valE), .out(multiplexer_2_out), .sel(decoder_1_out1));
  Multiplexer #(.width(64)) multiplexer_3 (.in0(valM), .in1(valE), .out(multiplexer_3_out), .sel(decoder_1_out2));
  Multiplexer #(.width(64)) multiplexer_4 (.in0(valM), .in1(valE), .out(multiplexer_4_out), .sel(decoder_1_out3));
  Multiplexer #(.width(64)) multiplexer_5 (.in0(valM), .in1(valE), .out(multiplexer_5_out), .sel(decoder_1_out4));
  Multiplexer #(.width(64)) multiplexer_6 (.in0(valM), .in1(valE), .out(multiplexer_6_out), .sel(decoder_1_out5));
  Multiplexer #(.width(64)) multiplexer_7 (.in0(valM), .in1(valE), .out(multiplexer_7_out), .sel(decoder_1_out6));
  Multiplexer #(.width(64)) multiplexer_8 (.in0(valM), .in1(valE), .out(multiplexer_8_out), .sel(decoder_1_out7));
  Multiplexer #(.width(64)) multiplexer_9 (.in0(valM), .in1(valE), .out(multiplexer_9_out), .sel(decoder_1_out8));
  Multiplexer #(.width(64)) multiplexer_10 (.in0(valM), .in1(valE), .out(multiplexer_10_out), .sel(decoder_1_out9));
  Multiplexer #(.width(64)) multiplexer_11 (.in0(valM), .in1(valE), .out(multiplexer_11_out), .sel(decoder_1_out10));
  Multiplexer #(.width(64)) multiplexer_12 (.in0(valM), .in1(valE), .out(multiplexer_12_out), .sel(decoder_1_out11));
  Multiplexer #(.width(64)) multiplexer_13 (.in0(valM), .in1(valE), .out(multiplexer_13_out), .sel(decoder_1_out12));
  Multiplexer #(.width(64)) multiplexer_14 (.in0(valM), .in1(valE), .out(multiplexer_14_out), .sel(decoder_1_out13));
  Multiplexer #(.width(64)) multiplexer_15 (.in0(valM), .in1(valE), .out(multiplexer_15_out), .sel(decoder_1_out14));
  Register #(.width(64)) rax (.D(multiplexer_1_out), .en(or_1_out), .clk(clk), .Q(rax_q));  // open: clr
  Register #(.width(64)) rcx (.D(multiplexer_2_out), .en(or_2_out), .clk(clk), .Q(rcx_q));  // open: clr
  Register #(.width(64)) rdx (.D(multiplexer_3_out), .en(or_3_out), .clk(clk), .Q(rdx_q));  // open: clr
  Register #(.width(64)) rbx (.D(multiplexer_4_out), .en(or_4_out), .clk(clk), .Q(rbx_q));  // open: clr
  Register #(.width(64)) rsp (.D(multiplexer_5_out), .en(or_5_out), .clk(clk), .Q(rsp_q));  // open: clr
  Register #(.width(64)) rbp (.D(multiplexer_6_out), .en(or_6_out), .clk(clk), .Q(rbp_q));  // open: clr
  Register #(.width(64)) rsi (.D(multiplexer_7_out), .en(or_7_out), .clk(clk), .Q(rsi_q));  // open: clr
  Register #(.width(64)) rdi (.D(multiplexer_8_out), .en(or_8_out), .clk(clk), .Q(rdi_q));  // open: clr
  Register #(.width(64)) r8 (.D(multiplexer_9_out), .en(or_9_out), .clk(clk), .Q(r8_q));  // open: clr
  Register #(.width(64)) r9 (.D(multiplexer_10_out), .en(or_10_out), .clk(clk), .Q(r9_q));  // open: clr
  Register #(.width(64)) r10 (.D(multiplexer_11_out), .en(or_11_out), .clk(clk), .Q(r10_q));  // open: clr
  Register #(.width(64)) r11 (.D(multiplexer_12_out), .en(or_12_out), .clk(clk), .Q(r11_q));  // open: clr
  Register #(.width(64)) r12 (.D(multiplexer_13_out), .en(or_13_out), .clk(clk), .Q(r12_q));  // open: clr
  Register #(.width(64)) r13 (.D(multiplexer_14_out), .en(or_14_out), .clk(clk), .Q(r13_q));  // open: clr
  Register #(.width(64)) r14 (.D(multiplexer_15_out), .en(or_15_out), .clk(clk), .Q(r14_q));  // open: clr
  Multiplexer #(.select(4), .width(64)) multiplexer_16 (
    .in0(rax_q), .in1(rcx_q), .in2(rdx_q), .in3(rbx_q), .in4(rsp_q), .in5(rbp_q), .in6(rsi_q), .in7(rdi_q),
    .in8(r8_q), .in9(r9_q), .in10(r10_q), .in11(r11_q), .in12(r12_q), .in13(r13_q), .in14(r14_q), .out(valA),
    .sel(srcA));  // open: in15
  Multiplexer #(.select(4), .width(64)) multiplexer_17 (
    .in0(rax_q), .in1(rcx_q), .in2(rdx_q), .in3(rbx_q), .in4(rsp_q), .in5(rbp_q), .in6(rsi_q), .in7(rdi_q),
    .in8(r8_q), .in9(r9_q), .in10(r10_q), .in11(r11_q), .in12(r12_q), .in13(r13_q), .in14(r14_q), .out(valB),
    .sel(srcB));  // open: in15
endmodule

module srcA (
  input  [3:0] icode,
  input  [3:0] rA,
  output [3:0] src_A
);

  wire call_out, Opq_out, or_1_out, or_2_out, popq_out, pushq_out, ret_out, rmmovq_out, rrmovq_out;
  wire [3:0] multiplexer_1_out;

  and rrmovq (rrmovq_out, ~icode[3], ~icode[2], icode[1], ~icode[0]);  // AND_Gate
  and rmmovq (rmmovq_out, ~icode[3], icode[2], ~icode[1], ~icode[0]);  // AND_Gate
  and Opq (Opq_out, ~icode[3], icode[2], icode[1], ~icode[0]);  // AND_Gate
  and pushq (pushq_out, icode[3], ~icode[2], icode[1], ~icode[0]);  // AND_Gate
  and call (call_out, icode[3], ~icode[2], ~icode[1], ~icode[0]);  // AND_Gate
  and ret (ret_out, icode[3], ~icode[2], ~icode[1], icode[0]);  // AND_Gate
  and popq (popq_out, icode[3], ~icode[2], icode[1], icode[0]);  // AND_Gate
  or or_1 (or_1_out, rrmovq_out, rmmovq_out, Opq_out, pushq_out);
  or or_2 (or_2_out, call_out, ret_out, popq_out);
  Multiplexer #(.width(4)) multiplexer_1 (.in0(4'b1111), .in1(4'b0100), .out(multiplexer_1_out), .sel(or_2_out));
  Multiplexer #(.width(4)) multiplexer_2 (.in0(multiplexer_1_out), .in1(rA), .out(src_A), .sel(or_1_out));
endmodule

module srcB (
  input  [3:0] icode,
  input  [3:0] rB,
  output [3:0] src_B
);

  wire call_out, mrmovq_out, Opq_out, or_1_out, or_2_out, popq_out, pushq_out, ret_out, rmmovq_out,
       rrmovq_out;
  wire [3:0] multiplexer_1_out;

  and call (call_out, icode[3], ~icode[2], ~icode[1], ~icode[0]);  // AND_Gate
  and ret (ret_out, icode[3], ~icode[2], ~icode[1], icode[0]);  // AND_Gate
  and popq (popq_out, icode[3], ~icode[2], icode[1], icode[0]);  // AND_Gate
  and pushq (pushq_out, icode[3], ~icode[2], icode[1], ~icode[0]);  // AND_Gate
  and rrmovq (rrmovq_out, ~icode[3], ~icode[2], icode[1], ~icode[0]);  // AND_Gate
  and rmmovq (rmmovq_out, ~icode[3], icode[2], ~icode[1], ~icode[0]);  // AND_Gate
  and Opq (Opq_out, ~icode[3], icode[2], icode[1], ~icode[0]);  // AND_Gate
  and mrmovq (mrmovq_out, ~icode[3], icode[2], ~icode[1], icode[0]);  // AND_Gate
  or or_1 (or_1_out, call_out, ret_out, popq_out, pushq_out);
  or or_2 (or_2_out, rrmovq_out, rmmovq_out, Opq_out, mrmovq_out);
  Multiplexer #(.width(4)) multiplexer_1 (.in0(4'b1111), .in1(4'b0100), .out(multiplexer_1_out), .sel(or_1_out));
  Multiplexer #(.width(4)) multiplexer_2 (.in0(multiplexer_1_out), .in1(rB), .out(src_B), .sel(or_2_out));
endmodule

module dstM (
  input  [3:0] icode,
  input  [3:0] rA,
  output [3:0] dst_M
);

  wire ir_out, mr_out, Opq_out, or_1_out, popq_out, rr_out;

  and rr (rr_out, ~icode[3], ~icode[2], icode[1], ~icode[0]);  // AND_Gate
  and ir (ir_out, ~icode[3], ~icode[2], icode[1], icode[0]);  // AND_Gate
  and mr (mr_out, ~icode[3], icode[2], ~icode[1], icode[0]);  // AND_Gate
  and popq (popq_out, icode[3], ~icode[2], icode[1], icode[0]);  // AND_Gate
  and Opq (Opq_out, ~icode[3], icode[2], icode[1], ~icode[0]);  // AND_Gate
  or or_1 (or_1_out, rr_out, ir_out, mr_out, popq_out, Opq_out);
  Multiplexer #(.width(4)) multiplexer_1 (.in0(4'b1111), .in1(rA), .out(dst_M), .sel(or_1_out));
endmodule

module dstE (
  input  Cnd,
  input  [3:0] icode,
  input  [3:0] rB,
  output [3:0] dst_E
);

  wire call_out, or_1_out, popq_out, pushq_out, ret_out;
  wire [3:0] multiplexer_1_out;

  and call (call_out, icode[3], ~icode[2], ~icode[1], ~icode[0]);  // AND_Gate
  and ret (ret_out, icode[3], ~icode[2], ~icode[1], icode[0]);  // AND_Gate
  and popq (popq_out, icode[3], ~icode[2], icode[1], icode[0]);  // AND_Gate
  and pushq (pushq_out, icode[3], ~icode[2], icode[1], ~icode[0]);  // AND_Gate
  or or_1 (or_1_out, call_out, ret_out, popq_out, pushq_out);
  Multiplexer #(.width(4)) multiplexer_1 (.in0(4'b1111), .in1(4'b0100), .out(multiplexer_1_out), .sel(or_1_out));
  Multiplexer #(.width(4)) multiplexer_2 (.in0(multiplexer_1_out), .in1(rB), .out(dst_E), .sel(Cnd));
endmodule
