// Logisim project MemoryLab6.circ as structural Verilog: 6 circuits, main circuit Memory
module Memory (
  input  [3:0] icode,
  input  [63:0] valE,
  input  [63:0] valA,
  input  [11:0] valP,
  output [63:0] valM
);

  wire clk_out, memread_1_reade, memwrite_1_writee;
  wire [11:0] memaddr_1_addrin;
  wire [63:0] memdata_1_datain;

  MemWrite memwrite_1 (.icode(icode), .WriteE(memwrite_1_writee));
  MemRead memread_1 (.icode(icode), .ReadE(memread_1_reade));
  MemAddr memaddr_1 (.icode(icode), .valE(valE), .valA(valA), .AddrIn(memaddr_1_addrin));
  Clock clk (.out(clk_out));
  MemData memdata_1 (.icode(icode), .valA(valA), .valP(valP), .DataIn(memdata_1_datain));
  DataMemory datamemory_1 (
    .mwrite(memwrite_1_writee), .mread(memread_1_reade), .mAddress(memaddr_1_addrin),
    .mData(memdata_1_datain), .clk(clk_out), .valM(valM));
endmodule

module DataMemory (
  input  mwrite,
  input  mread,
  input  [11:0] mAddress,
  input  [63:0] mData,
  input  clk,
  output [63:0] valM
);

  wire decoder_1_out0, decoder_1_out1, decoder_1_out2, decoder_1_out3, decoder_1_out4, decoder_1_out5,
       decoder_1_out6, decoder_1_out7;
  wire [2:0] counter_1_q;
  wire [7:0] multiplexer_1_out, ram_1_dout;
  wire [11:0] adder_1_out;

  Counter #(.max('h7), .width(3)) counter_1 (.clk(clk), .Q(counter_1_q));  // open: clr, load, up, count, D, carry
  Adder #(.width(12)) adder_1 (.a(mAddress), .b({{9{1'b0}}, counter_1_q}), .out(adder_1_out));  // open: cin, cout
  Multiplexer #(.select(3), .width(8)) multiplexer_1 (
    .in0(mData[7:0]), .in1(mData[15:8]), .in2(mData[23:16]), .in3(mData[31:24]), .in4(mData[39:32]),
    .in5(mData[47:40]), .in6(mData[55:48]), .in7(mData[63:56]), .out(multiplexer_1_out), .sel(counter_1_q));
  RAM #(.addrWidth(12)) ram_1 (
    .addr(adder_1_out), .we(mwrite), .oe(mread), .clk(clk), .din(multiplexer_1_out), .dout(ram_1_dout));
  Decoder #(.select(3)) decoder_1 (
    .out0(decoder_1_out0), .out1(decoder_1_out1), .out2(decoder_1_out2), .out3(decoder_1_out3),
    .out4(decoder_1_out4), .out5(decoder_1_out5), .out6(decoder_1_out6), .out7(decoder_1_out7),
    .sel(counter_1_q));  // open: en
  Register register_1 (.D(ram_1_dout), .en(decoder_1_out0), .clk(clk), .Q(valM[7:0]));  // open: clr
  Register register_2 (.D(ram_1_dout), .en(decoder_1_out1), .clk(clk), .Q(valM[15:8]));  // open: clr
  Register register_3 (.D(ram_1_dout), .en(decoder_1_out2), .clk(clk), .Q(valM[23:16]));  // open: clr
  Register register_4 (.D(ram_1_dout), .en(decoder_1_out3), .clk(clk), .Q(valM[31:24]));  // open: clr
  Register register_5 (.D(ram_1_dout), .en(decoder_1_out4), .clk(clk), .Q(valM[39:32]));  // open: clr
  Register register_6 (.D(ram_1_dout), .en(decoder_1_out5), .clk(clk), .Q(valM[47:40]));  // open: clr
  Register register_7 (.D(ram_1_dout), .en(decoder_1_out6), .clk(clk), .Q(valM[55:48]));  // open: clr
  Register register_8 (.D(ram_1_dout), .en(decoder_1_out7), .clk(clk), .Q(valM[63:56]));  // open: clr
endmodule

module MemData (
  input  [3:0] icode,
  input  [63:0] valA,
  input  [11:0] valP,
  output [63:0] DataIn
);

  wire call_out, or_1_out, push_out, rm_out, xor_1_out;
  wire [63:0] multiplexer_1_out;

  and rm (rm_out, ~icode[3], icode[2], ~icode[1], ~icode[0]);  // AND_Gate
  and push (push_out, icode[3], ~icode[2], icode[1], ~icode[0]);  // AND_Gate
  and call (call_out, icode[3], ~icode[2], ~icode[1], ~icode[0]);  // AND_Gate
  or or_1 (or_1_out, rm_out, push_out);
  Multiplexer #(.width(64)) multiplexer_1 (
    .in0(valA), .in1({{52{1'b0}}, valP}), .out(multiplexer_1_out), .sel(call_out));
  xor xor_1 (xor_1_out, or_1_out, call_out);
  Multiplexer #(.width(64)) multiplexer_2 (.in1(multiplexer_1_out), .out(DataIn), .sel(xor_1_out));  // open: in0
endmodule

module MemAddr (
  input  [3:0] icode,
  input  [63:0] valE,
  input  [63:0] valA,
  output [11:0] AddrIn
);

  wire call_out, mr_out, or_1_out, pop_out, push_out, ret_out, rm_out, xor_1_out;
  wire [11:0] multiplexer_1_out;

  and rm (rm_out, ~icode[3], icode[2], ~icode[1], ~icode[0]);  // AND_Gate
  and push (push_out, icode[3], ~icode[2], icode[1], ~icode[0]);  // AND_Gate
  and call (call_out, icode[3], ~icode[2], ~icode[1], ~icode[0]);  // AND_Gate
  and mr (mr_out, ~icode[3], icode[2], ~icode[1], icode[0]);  // AND_Gate
  and pop (pop_out, icode[3], ~icode[2], icode[1], icode[0]);  // AND_Gate
  and ret (ret_out, icode[3], ~icode[2], ~icode[1], icode[0]);  // AND_Gate
  or or_1 (or_1_out, rm_out, push_out, call_out, mr_out, pop_out);
  Multiplexer #(.width(12)) multiplexer_1 (.in0(valE[11:0]), .in1(valA[11:0]), .out(multiplexer_1_out), .sel(ret_out));
  xor xor_1 (xor_1_out, or_1_out, ret_out);
  Multiplexer #(.width(12)) multiplexer_2 (.in1(multiplexer_1_out), .out(AddrIn), .sel(xor_1_out));  // open: in0
endmodule

module MemWrite (
  input  [3:0] icode,
  output WriteE
);

  wire call_out, push_out, rm_out;

  and rm (rm_out, ~icode[3], icode[2], ~icode[1], ~icode[0]);  // AND_Gate
  and push (push_out, icode[3], ~icode[2], icode[1], ~icode[0]);  // AND_Gate
  and call (call_out, icode[3], ~icode[2], ~icode[1], ~icode[0]);  // AND_Gate
  or or_1 (WriteE, rm_out, push_out, call_out);
endmodule

module MemRead (
  input  [3:0] icode,
  output ReadE
);

  wire mr_out, pop_out, ret_out;

  and mr (mr_out, ~icode[3], icode[2], ~icode[1], icode[0]);  // AND_Gate
  and ret (ret_out, icode[3], ~icode[2], ~icode[1], icode[0]);  // AND_Gate
  and pop (pop_out, icode[3], ~icode[2], icode[1], icode[0]);  // AND_Gate
  or or_1 (ReadE, mr_out, ret_out, pop_out);
endmodule
