// Logisim project Execute.circ as structural Verilog: 8 circuits, main circuit Execute
module Execute (
  input  [3:0] icode,
  input  [3:0] ifun,
  input  [63:0] valA,
  input  [63:0] valB,
  input  [63:0] valC,
  output [63:0] valE,
  output Cnd
);

  wire clk_out, setcc_1_set;
  wire [1:0] alu_fun_1_fn;
  wire [2:0] cc_1_code;
  wire [63:0] alu_a_1_a, alu_b_1_b;

  Clock clk (.out(clk_out));
  ALU_A alu_a_1 (.valA(valA), .valC(valC), .icode(icode), .A(alu_a_1_a));
  ALU_B alu_b_1 (.valB(valB), .icode(icode), .B(alu_b_1_b));
  ALU_fun alu_fun_1 (.ifun(ifun), .icode(icode), .fn(alu_fun_1_fn));
  SetCC setcc_1 (.icode(icode), .set(setcc_1_set));
  ALU alu_1 (.A(alu_a_1_a), .B(alu_b_1_b), .fn(alu_fun_1_fn), .valE(valE));
  CC cc_1 (.SetCC(setcc_1_set), .valE(valE), .A(alu_a_1_a), .B(alu_b_1_b), .clk(clk_out), .code(cc_1_code));
  cond cond_1 (.code(cc_1_code), .ifun(ifun), .Cnd(Cnd));
endmodule

module ALU (
  input  [63:0] A,
  input  [63:0] B,
  input  [1:0] fn,
  output [63:0] valE
);

  wire and_2_out;
  wire [63:0] and_1_out, multiplexer_1_out, multiplexer_2_out, not_1_out, xor_1_out;

  assign and_1_out = A & B;  // AND_Gate and_1, 64 bits wide
  assign xor_1_out = A ^ B;  // XOR_Gate xor_1, 64 bits wide
  assign not_1_out = ~B;  // NOT_Gate not_1, 64 bits wide
  and and_2 (and_2_out, fn[0], ~fn[1]);  // AND_Gate
  Multiplexer #(.select(2), .width(64)) multiplexer_1 (
    .in0(A), .in1(A), .in2(and_1_out), .in3(xor_1_out), .out(multiplexer_1_out), .sel(fn));
  Multiplexer #(.select(2), .width(64)) multiplexer_2 (
    .in0(B), .in1(not_1_out), .in2({64{1'b0}}), .in3({64{1'b0}}), .out(multiplexer_2_out), .sel(fn));
  Adder #(.width(64)) adder_1 (
    .a(multiplexer_1_out), .b(multiplexer_2_out), .out(valE), .cin(and_2_out));  // open: cout

  // Notes on the sheet:
  //   A - B
  //   0 0 ADD
  //   0 1 SUB
  //   1 0 AND
  //   1 1 XOR
endmodule

module ALU_A (
  input  [63:0] valA,
  input  [63:0] valC,
  input  [3:0] icode,
  output [63:0] A
);

  wire [1:0] rom_1_data;

  ROM #(.addrWidth(4), .dataWidth(2)) rom_1 (.addr(icode), .data(rom_1_data));
  Multiplexer #(.select(2), .width(64)) multiplexer_1 (
    .in0(64'hfffffffffffffff8), .in1(64'h8), .in2(valA), .in3(valC), .out(A), .sel(rom_1_data));

  // Notes on the sheet:
  //   contents of rom_1 (hex, n*v repeats v):
  //   0 0 2 4*3 0 0 1 0 1
  //   used ROM to select from mux based on instruction
  //   Can be -8, 8, valA, or valC
  //   Shouldn't matter what is used for jXX, halt, and nop
endmodule

module ALU_B (
  input  [63:0] valB,
  input  [3:0] icode,
  output [63:0] B
);

  wire undriven;

  ROM #(.addrWidth(4), .dataWidth(1)) rom_1 (.addr(icode));  // open: data
  Multiplexer #(.width(64)) multiplexer_1 (.in0({64{1'b0}}), .in1(valB), .out(B), .sel(undriven));

  // Notes on the sheet:
  //   contents of rom_1 (hex, n*v repeats v):
  //   4*0 1 1 1 0 4*1
  //   used ROM to select from mux based on instruction
  //   Can be valB or 0
  //   Shouldn't matter what is used for jXX, halt, and nop
endmodule

module ALU_fun (
  input  [3:0] ifun,
  input  [3:0] icode,
  output [1:0] fn
);

  wire and_1_out;

  and and_1 (and_1_out, ~icode[0], icode[1], icode[2], ~icode[3]);  // AND_Gate
  Multiplexer #(.width(2)) multiplexer_1 (.in0(2'b00), .in1(ifun[1:0]), .out(fn), .sel(and_1_out));

  // Notes on the sheet:
  //   Use ADD unless OPq
  //   Shouldn't matter what is used for jXX, halt, and nop
  //   OPq
  //   0 0 ADD
  //   0 1 SUB
  //   1 0 AND
  //   1 1 XOR
endmodule

module SetCC (
  input  [3:0] icode,
  output set
);

  and and_1 (set, ~icode[0], icode[1], icode[2], ~icode[3]);  // AND_Gate

  // Notes on the sheet:
  //   OPq
endmodule

module CC (
  input  SetCC,
  input  [63:0] valE,
  input  [63:0] A,
  input  [63:0] B,
  input  clk,
  output [2:0] code
);

  wire comparator_3_lt, comparator_4_lt, comparator_5_lt, comparator_6_eq, comparator_7_eq;
  wire [2:0] comparator_1_eq;

  Comparator #(.width(64)) comparator_1 (.a(valE), .b({64{1'b0}}), .eq(comparator_1_eq[0]));  // open: gt, lt
  Comparator #(.width(64)) comparator_2 (.a(valE), .b({64{1'b0}}), .lt(comparator_1_eq[1]));  // open: gt, eq
  Comparator #(.width(64)) comparator_3 (.a(A), .b({64{1'b0}}), .lt(comparator_3_lt));  // open: gt, eq
  Comparator #(.width(64)) comparator_4 (.a(B), .b({64{1'b0}}), .lt(comparator_4_lt));  // open: gt, eq
  Comparator #(.width(64)) comparator_5 (.a(valE), .b({64{1'b0}}), .lt(comparator_5_lt));  // open: gt, eq
  Comparator #(.width(1)) comparator_6 (
    .a(comparator_3_lt), .b(comparator_4_lt), .eq(comparator_6_eq));  // open: gt, lt
  Comparator #(.width(1)) comparator_7 (
    .a(comparator_3_lt), .b(comparator_5_lt), .eq(comparator_7_eq));  // open: gt, lt
  and and_1 (comparator_1_eq[2], comparator_6_eq, ~comparator_7_eq);  // AND_Gate
  Register #(.width(3)) register_1 (.D(comparator_1_eq), .en(SetCC), .clk(clk), .Q(code));  // open: clr

  // Notes on the sheet:
  //   ZF: t == 0
  //   SF: t < 0
  //   OF: (a < 0 == b < 0) && (t < 0 != a < 0)
  //   Bit 0 - ZF
  //   Bit 1 - SF
  //   Bit 2 - OF
endmodule

module cond (
  input  [2:0] code,
  input  [3:0] ifun,
  output Cnd
);

  wire and_1_out, and_2_out, and_3_out, and_4_out, and_5_out, and_6_out, and_7_out, decoder_1_out0,
       decoder_1_out1, decoder_1_out2, decoder_1_out3, decoder_1_out4, decoder_1_out5, decoder_1_out6,
       or_1_out, xor_1_out;

  Decoder #(.enable("false"), .select(3)) decoder_1 (
    .out0(decoder_1_out0), .out1(decoder_1_out1), .out2(decoder_1_out2), .out3(decoder_1_out3),
    .out4(decoder_1_out4), .out5(decoder_1_out5), .out6(decoder_1_out6), .sel(ifun[2:0]));  // open: out7
  xor xor_1 (xor_1_out, code[1], code[2]);
  or or_1 (or_1_out, xor_1_out, code[0]);
  and and_1 (and_1_out, ~xor_1_out, ~code[0]);  // AND_Gate
  and and_2 (and_2_out, or_1_out, decoder_1_out1);
  and and_3 (and_3_out, xor_1_out, decoder_1_out2);
  and and_4 (and_4_out, code[0], decoder_1_out3);
  and and_5 (and_5_out, ~code[0], decoder_1_out4);  // AND_Gate
  and and_6 (and_6_out, ~xor_1_out, decoder_1_out5);  // AND_Gate
  and and_7 (and_7_out, and_1_out, decoder_1_out6);
  or or_2 (Cnd, decoder_1_out0, and_2_out, and_3_out, and_4_out, and_5_out, and_6_out, and_7_out);

  // Notes on the sheet:
  //   OF
  //   SF
  //   jmp: 1
  //   jle: (SF ^ OF) | ZF
  //   jl: SF ^ OF
  //   je: ZF
  //   jne: ~ZF
  //   jge: ~(SF ^ OF)
  //   ZF
  //   jg: ~(SF ^ OF) & ~ZF
endmodule
