// Logisim project Fetch.circ as structural Verilog: 7 circuits, main circuit Fetch
module Fetch (
  input  [11:0] PC,
  output [3:0] icode,
  output [3:0] ifun,
  output [3:0] rA,
  output [3:0] rB,
  output [63:0] valC,
  output [11:0] valP
);

  wire clk_out, need_regids_1_needregids, need_valc_1_needvalc;
  wire [7:0] instruction_memory_1_byte1, instruction_memory_1_byte2, instruction_memory_1_byte3,
       instruction_memory_1_byte4, instruction_memory_1_byte5, instruction_memory_1_byte6,
       instruction_memory_1_byte7, instruction_memory_1_byte8, instruction_memory_1_byte9;

  Clock clk (.out(clk_out));
  Instruction_Memory instruction_memory_1 (
    .PC(PC), .clk(clk_out), .Byte0({icode, ifun}), .Byte1(instruction_memory_1_byte1),
    .Byte2(instruction_memory_1_byte2), .Byte3(instruction_memory_1_byte3),
    .Byte4(instruction_memory_1_byte4), .Byte5(instruction_memory_1_byte5),
    .Byte6(instruction_memory_1_byte6), .Byte7(instruction_memory_1_byte7),
    .Byte8(instruction_memory_1_byte8), .Byte9(instruction_memory_1_byte9));
  Need_valC need_valc_1 (.icode(icode), .NeedValC(need_valc_1_needvalc));
  Need_Regids need_regids_1 (.icode(icode), .NeedRegids(need_regids_1_needregids));
  Align align_1 (
    .Byte1(instruction_memory_1_byte1), .Byte2(instruction_memory_1_byte2),
    .Byte3(instruction_memory_1_byte3), .Byte4(instruction_memory_1_byte4),
    .Byte5(instruction_memory_1_byte5), .Byte6(instruction_memory_1_byte6),
    .Byte7(instruction_memory_1_byte7), .Byte8(instruction_memory_1_byte8),
    .Byte9(instruction_memory_1_byte9), .NeedRegids(need_regids_1_needregids), .rA(rA), .rB(rB), .valC(valC));
  PC_Increment pc_increment_1 (
    .NeedValC(need_valc_1_needvalc), .NeedRegids(need_regids_1_needregids), .PC(PC), .valP(valP));

  // Notes on the sheet:
  //   Split
endmodule

module Instruction_Memory (
  input  [11:0] PC,
  input  clk,
  output [7:0] Byte0,
  output [7:0] Byte1,
  output [7:0] Byte2,
  output [7:0] Byte3,
  output [7:0] Byte4,
  output [7:0] Byte5,
  output [7:0] Byte6,
  output [7:0] Byte7,
  output [7:0] Byte8,
  output [7:0] Byte9
);

  wire counter_1_p2, decoder_1_out0, decoder_1_out1, decoder_1_out2, decoder_1_out3, decoder_1_out4,
       decoder_1_out5, decoder_1_out6, decoder_1_out7, decoder_1_out8, decoder_1_out9;
  wire [3:0] counter_1_p4;
  wire [7:0] rom_1_data;
  wire [11:0] adder_1_out;

  // Counter #(.max('h9), .width(4)) counter_1: pin names not known; wires that end beside it: clk, counter_1_p2, counter_1_p2, counter_1_p4
  ROM #(.addrWidth(12)) rom_1 (.addr(adder_1_out), .data(rom_1_data));
  Adder #(.width(12)) adder_1 (
    .a({4'b0000, PC[7:0]}), .b({{8{1'b0}}, counter_1_p4}), .out(adder_1_out));  // open: cin, cout
  Decoder #(.select(4)) decoder_1 (
    .out0(decoder_1_out0), .out1(decoder_1_out1), .out2(decoder_1_out2), .out3(decoder_1_out3),
    .out4(decoder_1_out4), .out5(decoder_1_out5), .out6(decoder_1_out6), .out7(decoder_1_out7),
    .out8(decoder_1_out8), .out9(decoder_1_out9), .sel(counter_1_p4));  // open: out10, out11, out12, out13, out14, out15, en
  Register register_1 (.D(rom_1_data), .en(decoder_1_out0), .clk(clk), .Q(Byte0));  // open: clr
  Register register_2 (.D(rom_1_data), .en(decoder_1_out1), .clk(clk), .Q(Byte1));  // open: clr
  Register register_3 (.D(rom_1_data), .en(decoder_1_out2), .clk(clk), .Q(Byte2));  // open: clr
  Register register_4 (.D(rom_1_data), .en(decoder_1_out3), .clk(clk), .Q(Byte3));  // open: clr
  Register register_5 (.D(rom_1_data), .en(decoder_1_out4), .clk(clk), .Q(Byte4));  // open: clr
  Register register_6 (.D(rom_1_data), .en(decoder_1_out5), .clk(clk), .Q(Byte5));  // open: clr
  Register register_7 (.D(rom_1_data), .en(decoder_1_out6), .clk(clk), .Q(Byte6));  // open: clr
  Register register_8 (.D(rom_1_data), .en(decoder_1_out7), .clk(clk), .Q(Byte7));  // open: clr
  Register register_9 (.D(rom_1_data), .en(decoder_1_out8), .clk(clk), .Q(Byte8));  // open: clr
  Register register_10 (.D(rom_1_data), .en(decoder_1_out9), .clk(clk), .Q(Byte9));  // open: clr

  // Notes on the sheet:
  //   contents of rom_1 (hex, n*v repeats v):
  //   30 f4 0 2 6*0 80 38 12*0 d 0 d 0 d 0 0 0 c0 0 c0 0 c0 4*0 b 0 b 0 b 0 0 0 a0 0 a0 0 a0 0 0 30 f7 18
  //   7*0 30 f6 4 7*0 80 56 7*0 90 30 f8 8 7*0 30 f9 1 7*0 63 0 62 66 70 87 7*0 50 a7 8*0 60 a0 60 87 61
  //   96 74 77 7*0 90
endmodule

module PC_Increment (
  input  NeedValC,
  input  NeedRegids,
  input  [11:0] PC,
  output [11:0] valP
);

  wire [11:0] adder_1_out, adder_2_out, multiplier_1_out;

  Multiplier #(.width(12)) multiplier_1 (
    .a({{11{1'b0}}, NeedValC}), .b(12'h8), .out(multiplier_1_out));  // open: cin, cout
  Adder #(.width(12)) adder_1 (.a(12'h1), .b({{11{1'b0}}, NeedRegids}), .out(adder_1_out));  // open: cin, cout
  Adder #(.width(12)) adder_2 (.a(multiplier_1_out), .b(adder_1_out), .out(adder_2_out));  // open: cin, cout
  Adder #(.width(12)) adder_3 (.a(adder_2_out), .b(PC), .out(valP));  // open: cin, cout
endmodule

module Need_valC (
  input  [3:0] icode,
  output NeedValC
);

  wire and_1_out, and_2_out, and_3_out, and_4_out, and_5_out;

  and and_1 (and_1_out, icode[0], icode[2], ~icode[1], ~icode[3]);  // AND_Gate
  and and_2 (and_2_out, ~icode[0], ~icode[2], icode[1], ~icode[3]);  // AND_Gate
  and and_3 (and_3_out, icode[0], ~icode[2], icode[1], ~icode[3]);  // AND_Gate
  and and_4 (and_4_out, icode[0], icode[2], icode[1], ~icode[3]);  // AND_Gate
  and and_5 (and_5_out, ~icode[0], ~icode[2], ~icode[1], icode[3]);  // AND_Gate
  or or_1 (NeedValC, and_1_out, and_2_out, and_3_out, and_4_out, and_5_out);

  // Notes on the sheet:
  //   irmovq (3)
  //   rmmovq (4)
  //   mrmovq (5)
  //   jXX (7)
  //   call (8)
endmodule

module Need_Regids (
  input  [3:0] icode,
  output NeedRegids
);

  wire and_1_out, and_2_out, and_3_out, and_4_out, and_5_out, and_6_out, and_7_out;

  and and_1 (and_1_out, ~icode[0], icode[1], ~icode[2], ~icode[3]);  // AND_Gate
  and and_2 (and_2_out, icode[0], icode[1], ~icode[2], ~icode[3]);  // AND_Gate
  and and_3 (and_3_out, ~icode[0], ~icode[1], icode[2], ~icode[3]);  // AND_Gate
  and and_4 (and_4_out, icode[0], ~icode[1], icode[2], ~icode[3]);  // AND_Gate
  and and_5 (and_5_out, ~icode[0], icode[1], icode[2], ~icode[3]);  // AND_Gate
  and and_6 (and_6_out, ~icode[0], icode[1], ~icode[2], icode[3]);  // AND_Gate
  and and_7 (and_7_out, icode[0], icode[1], ~icode[2], icode[3]);  // AND_Gate
  or or_1 (NeedRegids, and_1_out, and_2_out, and_3_out, and_4_out, and_5_out, and_6_out, and_7_out);

  // Notes on the sheet:
  //   irmovq (3)
  //   rmmovq (4)
  //   mrmovq (5)
  //   OPq (6)
  //   pushq (a)
  //   popq (b)
  //   rrmovq / cmovXX (2)
endmodule

module Instr_Valid (
  input  [3:0] icode,
  output InstrValid
);

  Comparator #(.mode("unsigned"), .width(4)) comparator_1 (.a(icode), .b(4'b1100), .lt(InstrValid));  // open: gt, eq
endmodule

module Align (
  input  [7:0] Byte1,
  input  [7:0] Byte2,
  input  [7:0] Byte3,
  input  [7:0] Byte4,
  input  [7:0] Byte5,
  input  [7:0] Byte6,
  input  [7:0] Byte7,
  input  [7:0] Byte8,
  input  [7:0] Byte9,
  input  NeedRegids,
  output [3:0] rA,
  output [3:0] rB,
  output [63:0] valC
);

  Multiplexer #(.width(8)) multiplexer_1 (.in0({8{1'b1}}), .in1(Byte1), .out({rA, rB}), .sel(NeedRegids));
  Multiplexer #(.width(8)) multiplexer_2 (.in0(Byte1), .in1(Byte2), .out(valC[7:0]), .sel(NeedRegids));
  Multiplexer #(.width(8)) multiplexer_3 (.in0(Byte2), .in1(Byte3), .out(valC[15:8]), .sel(NeedRegids));
  Multiplexer #(.width(8)) multiplexer_4 (.in0(Byte3), .in1(Byte4), .out(valC[23:16]), .sel(NeedRegids));
  Multiplexer #(.width(8)) multiplexer_5 (.in0(Byte4), .in1(Byte5), .out(valC[31:24]), .sel(NeedRegids));
  Multiplexer #(.width(8)) multiplexer_6 (.in0(Byte5), .in1(Byte6), .out(valC[39:32]), .sel(NeedRegids));
  Multiplexer #(.width(8)) multiplexer_7 (.in0(Byte6), .in1(Byte7), .out(valC[47:40]), .sel(NeedRegids));
  Multiplexer #(.width(8)) multiplexer_8 (.in0(Byte7), .in1(Byte8), .out(valC[55:48]), .sel(NeedRegids));
  Multiplexer #(.width(8)) multiplexer_9 (.in0(Byte8), .in1(Byte9), .out(valC[63:56]), .sel(NeedRegids));

  // Notes on the sheet:
  //   rA and rB set to 0xf if not needed
endmodule
