// Logisim project PCUpdate.circ as structural Verilog: 2 circuits, main circuit PCUpdate
module PCUpdate (
  input  [3:0] icode,
  input  [63:0] valP,
  input  [63:0] valM,
  input  [63:0] valC,
  output [63:0] out_5
);

  wire [1:0] log_1_r_valp;

  log log_1 (.icode(icode), .r_valP(log_1_r_valp[0]), .valM(log_1_r_valp[1]));
  Multiplexer #(.select(2), .width(64)) multiplexer_1 (
    .in1(valP), .in2(valM), .in3(valC), .out(out_5), .sel(log_1_r_valp));  // open: in0
endmodule

module log (
  input  [3:0] icode,
  output r_valP,
  output valM
);

  wire call_out, ir_cm_out, mr_out, op_out, or_2_out, popq_out, pushq_out, ret_out, rm_out, rr_out;

  and rr (rr_out, ~icode[3], ~icode[2], icode[1], ~icode[0]);  // AND_Gate
  and ir_cm (ir_cm_out, ~icode[3], ~icode[2], icode[1], icode[0]);  // AND_Gate
  and rm (rm_out, ~icode[3], icode[2], ~icode[1], ~icode[0]);  // AND_Gate
  and mr (mr_out, ~icode[3], icode[2], ~icode[1], icode[0]);  // AND_Gate
  and op (op_out, ~icode[3], icode[2], icode[1], ~icode[0]);  // AND_Gate
  and pushq (pushq_out, icode[3], ~icode[2], icode[1], ~icode[0]);  // AND_Gate
  and popq (popq_out, icode[3], ~icode[2], icode[1], icode[0]);  // AND_Gate
  and call (call_out, icode[3], ~icode[2], ~icode[1], ~icode[0]);  // AND_Gate
  and ret (ret_out, icode[3], ~icode[2], ~icode[1], icode[0]);  // AND_Gate
  // AND_Gate cmove has open pins: in0=icode[3], in1=icode[2], in2=icode[1], in3=icode[0], out=open
  or or_1 (valM, call_out, ret_out);
  or or_2 (or_2_out, rr_out, ir_cm_out, rm_out, mr_out, op_out, pushq_out, popq_out);
  or or_3 (r_valP, or_2_out, call_out);
endmodule
