// Logisim project WriteBack.circ as structural Verilog: 2 circuits, main circuit WriteBack
module WriteBack (
  input  [3:0] icode,
  input  [1:0] ifun,
  input  [63:0] valM,
  input  [63:0] valE,
  output [2:0] addr_rB_rsp_rA,
  output [63:0] valM_out,
  output [63:0] valE_out
);

  wire or_1_out, read_ra_1_rb, read_ra_1_rsp, read_ra_1_valid, read_ra_1_valm_ra;
  wire [63:0] controlled_buffer_4_out, controlled_buffer_5_out;

  read_rA read_ra_1 (
    .icode(icode), .ifun(ifun), .valM_rA(read_ra_1_valm_ra), .valid(read_ra_1_valid), .rsp(read_ra_1_rsp),
    .rB(read_ra_1_rb));
  assign addr_rB_rsp_rA[0] = read_ra_1_valid ? read_ra_1_valm_ra : 1'bz;  // Controlled_Buffer controlled_buffer_1
  assign addr_rB_rsp_rA[1] = read_ra_1_valid ? read_ra_1_rsp : 1'bz;  // Controlled_Buffer controlled_buffer_2
  assign addr_rB_rsp_rA[2] = read_ra_1_valid ? read_ra_1_rb : 1'bz;  // Controlled_Buffer controlled_buffer_3
  assign controlled_buffer_4_out = read_ra_1_valid ? valM : 64'bz;  // Controlled_Buffer controlled_buffer_4
  assign controlled_buffer_5_out = read_ra_1_valid ? valE : 64'bz;  // Controlled_Buffer controlled_buffer_5
  assign valM_out = addr_rB_rsp_rA[0] ? controlled_buffer_4_out : 64'bz;  // Controlled_Buffer controlled_buffer_6
  or or_1 (or_1_out, addr_rB_rsp_rA[1], addr_rB_rsp_rA[2]);
  assign valE_out = or_1_out ? controlled_buffer_5_out : 64'bz;  // Controlled_Buffer controlled_buffer_7
endmodule

module read_rA (
  input  [3:0] icode,
  input  [1:0] ifun,
  output valM_rA,
  output valid,
  output rsp,
  output rB
);

  wire call_out, ir_out, mr_out, op_out, or_1_out, or_2_out, or_3_out, or_6_out, popq_out, pushq_out,
       ret_out, rr_out;

  or or_1 (or_1_out, ifun[0], ifun[1]);
  or or_2 (or_2_out, ifun[0], ifun[1]);
  and rr (rr_out, ~icode[3], ~icode[2], icode[1], ~icode[0], ~or_1_out);  // AND_Gate
  and ir (ir_out, ~icode[3], ~icode[2], icode[1], icode[0]);  // AND_Gate
  and mr (mr_out, ~icode[3], icode[2], ~icode[1], icode[0]);  // AND_Gate
  and op (op_out, ~icode[3], icode[2], icode[1], ~icode[0]);  // AND_Gate
  and call (call_out, icode[3], ~icode[2], ~icode[1], ~icode[0]);  // AND_Gate
  and ret (ret_out, icode[3], ~icode[2], ~icode[1], icode[0]);  // AND_Gate
  and pushq (pushq_out, icode[3], ~icode[2], icode[1], ~icode[0]);  // AND_Gate
  and popq (popq_out, icode[3], ~icode[2], icode[1], icode[0]);  // AND_Gate
  and cmove (rB, ~icode[3], ~icode[2], icode[1], ~icode[0], or_2_out);  // AND_Gate
  or or_3 (or_3_out, rr_out, ir_out, mr_out, op_out);
  or or_4 (rsp, call_out, ret_out, pushq_out, popq_out);
  or or_5 (valid, or_3_out, or_6_out);
  or or_6 (or_6_out, rB, rsp);
  or or_7 (valM_rA, or_3_out, popq_out);
endmodule
